// Logisim project Logisim Design.circ as structural Verilog: 5 circuits, main circuit Processor
module Processor (
  input  in_1
);

  wire alu_1_zero_signal__for_branching, main_control_1_alu_source, main_control_1_branch,
       main_control_1_extension_operation, main_control_1_memory_read, main_control_1_memory_to_register,
       main_control_1_memory_write, main_control_1_register_destination, main_control_1_register_write,
       Take_Branch_or_No_out;
  wire [1:0] alu_control_1_alu_control_signal, main_control_1_aluopt_0;
  wire [2:0] multiplexer_1_out;
  wire [15:0] adder_1_out, adder_2_out, alu_1_output, bit_extender_1_out, multiplexer_2_out,
       multiplexer_3_out, multiplexer_4_out, Program_Counter_q, ram_1_data, registe_file_1_read_data_1,
       registe_file_1_read_data_2, rom_1_data;

  Register #(.width(16)) Program_Counter (.D(multiplexer_3_out), .Q(Program_Counter_q), .clr(in_1));  // open: en, clk
  ROM #(.addrWidth(16), .dataWidth(16)) rom_1 (.addr(Program_Counter_q), .data(rom_1_data));  // open: sel
  Main_Control main_control_1 (
    .Operation_Code(rom_1_data[15:14]), .Register_Write(main_control_1_register_write),
    .ALU_Source(main_control_1_alu_source), .Register_Destination(main_control_1_register_destination),
    .Memory_to_Register(main_control_1_memory_to_register), .Memory_Write(main_control_1_memory_write),
    .Branch(main_control_1_branch), .Extension_Operation(main_control_1_extension_operation),
    .Memory_Read(main_control_1_memory_read), .ALUopt_1(main_control_1_aluopt_0[1]),
    .ALUopt_0(main_control_1_aluopt_0[0]));
  Multiplexer #(.width(3), .enable("false")) multiplexer_1 (
    .in0(rom_1_data[10:8]), .in1(rom_1_data[7:5]), .out(multiplexer_1_out),
    .sel(main_control_1_register_destination));
  assign bit_extender_1_out = {{8{main_control_1_extension_operation}}, rom_1_data[7:0]};  // Bit_Extender bit_extender_1
  Registe_File registe_file_1 (
    .Read_Register_Address_1(rom_1_data[13:11]), .Read_Register_Address_2(rom_1_data[10:8]),
    .Write_Data(multiplexer_4_out), .Read_Data_1(registe_file_1_read_data_1),
    .Read_Data_2(registe_file_1_read_data_2), .Write_Register_Address(multiplexer_1_out),
    .Register_Write(main_control_1_register_write), .Clear(in_1));
  Adder #(.width(16)) adder_1 (.a(16'h1), .b(Program_Counter_q), .out(adder_1_out));  // open: cin, cout
  Adder #(.width(16)) adder_2 (.a(adder_1_out), .b(bit_extender_1_out), .out(adder_2_out));  // open: cin, cout
  Multiplexer #(.width(16), .enable("false")) multiplexer_2 (
    .in0(registe_file_1_read_data_2), .in1(bit_extender_1_out), .out(multiplexer_2_out),
    .sel(main_control_1_alu_source));
  ALU_Control alu_control_1 (
    .ALUopt(main_control_1_aluopt_0), .Function_Code(rom_1_data[4:0]),
    .ALU_Control_Signal(alu_control_1_alu_control_signal));
  and Take_Branch_or_No (Take_Branch_or_No_out, main_control_1_branch, alu_1_zero_signal__for_branching);
  ALU alu_1 (
    .Input(registe_file_1_read_data_1), .Input_2(multiplexer_2_out), .Output(alu_1_output),
    .Zero_Signal__for_branching(alu_1_zero_signal__for_branching),
    .ALU_Control_Signal(alu_control_1_alu_control_signal));
  Multiplexer #(.width(16), .enable("false")) multiplexer_3 (
    .in0(adder_1_out), .in1(adder_2_out), .out(multiplexer_3_out), .sel(Take_Branch_or_No_out));
  RAM #(.addrWidth(16), .dataWidth(16), .bus("separate")) ram_1 (
    .addr(alu_1_output), .din(registe_file_1_read_data_2), .data(ram_1_data),
    .str(main_control_1_memory_write), .ld(main_control_1_memory_read));  // open: sel, clk, clr
  Multiplexer #(.width(16), .enable("false")) multiplexer_4 (
    .in0(ram_1_data), .in1(alu_1_output), .out(multiplexer_4_out), .sel(main_control_1_memory_to_register));

  // Notes on the sheet:
  //   ROM
  //   contents of rom_1 (hex, n*v repeats v):
  //   0 1 100
  //   RAM
endmodule

module ALU (
  input  [15:0] Input,
  input  [15:0] Input_2,
  input  [1:0] ALU_Control_Signal,
  output Zero_Signal__for_branching,
  output [15:0] Output
);

  wire [15:0] adder_1_out, and_1_out, or_1_out, subtractor_1_out;

  Adder #(.width(16)) adder_1 (.a(Input), .b(Input_2), .out(adder_1_out));  // open: cin, cout
  Subtractor #(.width(16)) subtractor_1 (.a(Input), .b(Input_2), .out(subtractor_1_out));  // open: bin, bout
  assign and_1_out = Input & Input_2;  // AND_Gate and_1, 16 bits wide
  assign or_1_out = Input | Input_2;  // OR_Gate or_1, 16 bits wide
  Multiplexer #(.select(2), .width(16), .enable("false")) multiplexer_1 (
    .in0(adder_1_out), .in1(subtractor_1_out), .in2(and_1_out), .in3(or_1_out), .out(Output),
    .sel(ALU_Control_Signal));
  nor nor_1 (Zero_Signal__for_branching, Output[15], Output[14], Output[13], Output[12], Output[11], Output[10], Output[9], Output[8], Output[7], Output[6], Output[5], Output[4], Output[3], Output[2], Output[1], Output[0]);
endmodule

// Main Control Unit
module Main_Control (
  input  [1:0] Operation_Code,
  output Register_Write,
  output ALU_Source,
  output Register_Destination,
  output Memory_to_Register,
  output Memory_Write,
  output Branch,
  output Extension_Operation,
  output Memory_Read,
  output ALUopt_1,
  output ALUopt_0
);

  wire not_1_out, not_2_out, not_3_out, not_4_out;

  not not_1 (not_1_out, Operation_Code[0]);
  not not_2 (not_2_out, Operation_Code[1]);
  not not_3 (not_3_out, Operation_Code[1]);
  not not_4 (not_4_out, Operation_Code[0]);
  and R_Formats (ALUopt_1, not_1_out, not_2_out);
  and Load__lw (Memory_Read, Operation_Code[0], not_3_out);
  and Store__sw (Memory_Write, not_4_out, Operation_Code[1]);
  and beq (ALUopt_0, Operation_Code[0], Operation_Code[1]);
  or or_1 (Register_Write, ALUopt_1, Memory_Read);
  or or_2 (ALU_Source, Memory_Read, Memory_Write);
  or or_3 (Extension_Operation, Memory_Read, Memory_Write, ALUopt_0);

  assign Branch = ALUopt_0;
  assign Memory_to_Register = Memory_Read;
  assign Register_Destination = ALUopt_1;
endmodule

// ALU Control Unit
module ALU_Control (
  input  [1:0] ALUopt,
  input  [4:0] Function_Code,
  output [1:0] ALU_Control_Signal
);

  Multiplexer #(.width(2), .enable("false")) multiplexer_1 (
    .in0(ALUopt), .in1(Function_Code[1:0]), .out(ALU_Control_Signal), .sel(ALUopt[1]));
endmodule

// 16-bit 8-register Register File
module Registe_File (
  input  [2:0] Read_Register_Address_1,
  input  [2:0] Read_Register_Address_2,
  input  [2:0] Write_Register_Address,
  input  Register_Write,
  input  Clear,
  input  [15:0] Write_Data,
  output [15:0] Read_Data_1,
  output [15:0] Read_Data_2
);

  wire and_1_out, and_2_out, and_3_out, and_4_out, and_5_out, and_6_out, and_7_out, and_8_out,
       decoder_1_out0, decoder_1_out1, decoder_1_out2, decoder_1_out3, decoder_1_out4, decoder_1_out5,
       decoder_1_out6, decoder_1_out7;
  wire [15:0] register_1_q, register_2_q, register_3_q, register_4_q, register_5_q, register_6_q,
       register_7_q, register_8_q;

  Decoder #(.select(3)) decoder_1 (
    .out0(decoder_1_out0), .out1(decoder_1_out1), .out2(decoder_1_out2), .out3(decoder_1_out3),
    .out4(decoder_1_out4), .out5(decoder_1_out5), .out6(decoder_1_out6), .out7(decoder_1_out7),
    .sel(Write_Register_Address));  // open: en
  and and_1 (and_1_out, decoder_1_out0, Register_Write);
  and and_2 (and_2_out, decoder_1_out1, Register_Write);
  and and_3 (and_3_out, decoder_1_out2, Register_Write);
  and and_4 (and_4_out, decoder_1_out3, Register_Write);
  and and_5 (and_5_out, decoder_1_out4, Register_Write);
  and and_6 (and_6_out, decoder_1_out5, Register_Write);
  and and_7 (and_7_out, decoder_1_out6, Register_Write);
  and and_8 (and_8_out, decoder_1_out7, Register_Write);
  Register #(.width(16)) register_1 (.D(Write_Data), .Q(register_1_q), .clk(and_1_out), .clr(Clear));  // open: en
  Register #(.width(16)) register_2 (.D(Write_Data), .Q(register_2_q), .clk(and_2_out), .clr(Clear));  // open: en
  Register #(.width(16)) register_3 (.D(Write_Data), .Q(register_3_q), .clk(and_3_out), .clr(Clear));  // open: en
  Register #(.width(16)) register_4 (.D(Write_Data), .Q(register_4_q), .clk(and_4_out), .clr(Clear));  // open: en
  Register #(.width(16)) register_5 (.D(Write_Data), .Q(register_5_q), .clk(and_5_out), .clr(Clear));  // open: en
  Register #(.width(16)) register_6 (.D(Write_Data), .Q(register_6_q), .clk(and_6_out), .clr(Clear));  // open: en
  Register #(.width(16)) register_7 (.D(Write_Data), .Q(register_7_q), .clk(and_7_out), .clr(Clear));  // open: en
  Register #(.width(16)) register_8 (.D(Write_Data), .Q(register_8_q), .clk(and_8_out), .clr(Clear));  // open: en
  Multiplexer #(.select(3), .width(16)) multiplexer_1 (
    .in0(register_1_q), .in1(register_2_q), .in2(register_3_q), .in3(register_4_q), .in4(register_5_q),
    .in5(register_6_q), .in6(register_7_q), .in7(register_8_q), .out(Read_Data_1),
    .sel(Read_Register_Address_1));  // open: en
  Multiplexer #(.select(3), .width(16)) multiplexer_2 (
    .in0(register_1_q), .in1(register_2_q), .in2(register_3_q), .in3(register_4_q), .in4(register_5_q),
    .in5(register_6_q), .in6(register_7_q), .in7(register_8_q), .out(Read_Data_2),
    .sel(Read_Register_Address_2));  // open: en
endmodule
